// Logisim project renata_rodrigues_16_bits.circ as structural Verilog: 15 circuits, main circuit main
module main (
);

  wire and_1_out, comparator_1_eq, Data_Address, flags_1_out_6, flags_1_out_7, flags_1_out_8, flags_1_out_9,
       Input_Output, ioe, ios, monitor_1_out_6, monitor_1_out_7, or_1_out, portio_1_p1, teclado_1_out_8,
       teclado_1_out_9, uc_1_acce, uc_1_accs, uc_1_bus1e, uc_1_flagss, uc_1_iare, uc_1_iars, uc_1_init,
       uc_1_irs, uc_1_mars, uc_1_r0e, uc_1_r0s, uc_1_r1e, uc_1_r1s, uc_1_r2e, uc_1_r2s, uc_1_r3e, uc_1_r3s,
       uc_1_rame, uc_1_rams, uc_1_tmps, ula_1_a_equal_b, ula_1_a_larger_than_b, ula_1_c_out, ula_1_zero;
  wire [2:0] uc_1_to_ula;
  wire [6:0] keyboard_1_data, monitor_1_out_5;
  wire [15:0] ACC_q, bus_1_1_out_3, controlled_buffer_1_out, controlled_buffer_7_out, IAR_q, IR_q, MAR_q,
       register_1_q, register_2_q, register_3_q, register_4_q, TMP_q, ula_1_resultado;

  Register #(.width(16)) TMP (.D(controlled_buffer_1_out), .Q(TMP_q), .clk(uc_1_tmps));  // open: en, clr
  bus_1 bus_1_1 (.in_1(TMP_q), .out_3(bus_1_1_out_3), .in_2(uc_1_bus1e));
  ULA ula_1 (
    .A(controlled_buffer_1_out), .B(bus_1_1_out_3), .resultado(ula_1_resultado), .operacao(uc_1_to_ula),
    .c_out(ula_1_c_out), .a_larger_than_b(ula_1_a_larger_than_b), .a_equal_b(ula_1_a_equal_b),
    .zero(ula_1_zero));
  flags flags_1 (
    .c_out(ula_1_c_out), .larger(ula_1_a_larger_than_b), .equal(ula_1_a_equal_b), .zero(ula_1_zero),
    .out_6(flags_1_out_6), .out_7(flags_1_out_7), .out_8(flags_1_out_8), .out_9(flags_1_out_9),
    .set(uc_1_flagss));
  Register #(.width(16)) ACC (.D(ula_1_resultado), .Q(ACC_q), .clk(uc_1_accs));  // open: en, clr
  assign controlled_buffer_1_out = uc_1_acce ? ACC_q : 16'bz;  // Controlled_Buffer controlled_buffer_1
  teclado teclado_1 (
    .in_2(ioe), .in_4(ios), .in_5(Data_Address), .in_6(Input_Output), .in_1(controlled_buffer_1_out),
    .out_7(controlled_buffer_1_out), .in_3(keyboard_1_data), .out_8(teclado_1_out_8), .out_9(teclado_1_out_9));
  assign controlled_buffer_1_out = uc_1_r0e ? register_1_q : 16'bz;  // Controlled_Buffer controlled_buffer_2
  Register #(.width(16)) register_1 (.D(controlled_buffer_1_out), .Q(register_1_q), .clk(uc_1_r0s));  // open: en, clr
  Register #(.width(16)) IAR (.D(controlled_buffer_1_out), .Q(IAR_q), .clk(uc_1_iars));  // open: en, clr
  assign controlled_buffer_1_out = uc_1_iare ? IAR_q : 16'bz;  // Controlled_Buffer controlled_buffer_3
  Keyboard keyboard_1 (.clk(teclado_1_out_8), .re(teclado_1_out_9), .data(keyboard_1_data));  // open: clr, avail
  assign controlled_buffer_1_out = uc_1_r1e ? register_2_q : 16'bz;  // Controlled_Buffer controlled_buffer_4
  Register #(.width(16)) register_2 (.D(controlled_buffer_1_out), .Q(register_2_q), .clk(uc_1_r1s));  // open: en, clr
  UC uc_1 (
    .to_ULA(uc_1_to_ula), .c_out(flags_1_out_6), .a_larger(flags_1_out_7), .equal(flags_1_out_8),
    .zero(flags_1_out_9), .flagss(uc_1_flagss), .Bus1e(uc_1_bus1e), .TMPs(uc_1_tmps), .R0s(uc_1_r0s),
    .R0e(uc_1_r0e), .R1s(uc_1_r1s), .R1e(uc_1_r1e), .R2s(uc_1_r2s), .R2e(uc_1_r2e), .R3s(uc_1_r3s),
    .R3e(uc_1_r3e), .MARs(uc_1_mars), .ACCs(uc_1_accs), .ACCe(uc_1_acce), .IARs(uc_1_iars), .IARe(uc_1_iare),
    .from_IR(IR_q), .IRs(uc_1_irs), .Input_Output(Input_Output), .Data_Address(Data_Address), .Ioe(ioe),
    .IOs(ios), .RAMs(uc_1_rams), .RAMe(uc_1_rame), .init(uc_1_init));
  LED led_1 (.in(uc_1_init));
  Register #(.width(16)) IR (.D(controlled_buffer_1_out), .Q(IR_q), .clk(uc_1_irs));  // open: en, clr
  assign controlled_buffer_1_out = uc_1_r2e ? register_3_q : 16'bz;  // Controlled_Buffer controlled_buffer_5
  Register #(.width(16)) register_3 (.D(controlled_buffer_1_out), .Q(register_3_q), .clk(uc_1_r2s));  // open: en, clr
  monitor monitor_1 (
    .in_2(ios), .in_3(Data_Address), .in_4(Input_Output), .in_1(controlled_buffer_1_out),
    .out_5(monitor_1_out_5), .out_6(monitor_1_out_6), .out_7(monitor_1_out_7));
  TTY tty_1 (.data(monitor_1_out_5), .clk(monitor_1_out_6), .we(monitor_1_out_7));  // open: clr
  // Probe on MAR_q
  Register #(.width(16)) register_4 (.D(controlled_buffer_1_out), .Q(register_4_q), .clk(uc_1_r3s));  // open: en, clr
  Register #(.width(16)) MAR (.D(controlled_buffer_1_out), .Q(MAR_q), .clk(uc_1_mars));  // open: en, clr
  assign controlled_buffer_1_out = uc_1_r3e ? register_4_q : 16'bz;  // Controlled_Buffer controlled_buffer_6
  or or_1 (or_1_out, uc_1_rams, uc_1_rame);
  RAM #(.addrWidth(16), .dataWidth(16), .databus("bidir")) ram_1 (
    .addr(MAR_q), .we(uc_1_rams), .oe(uc_1_rame), .clk(or_1_out), .data(controlled_buffer_1_out));
  Comparator #(.width(16)) comparator_1 (.a(controlled_buffer_1_out), .b(16'h2), .eq(comparator_1_eq));  // open: gt, lt
  and and_1 (and_1_out, ios, Data_Address, Input_Output);
  assign controlled_buffer_7_out = ios ? controlled_buffer_1_out : 16'bz;  // Controlled_Buffer controlled_buffer_7
  // PortIO #(.number(16)) portio_1: pin names not known; wires that end beside it: portio_1_p1, controlled_buffer_7_out
  Register #(.width(1)) register_5 (.D(comparator_1_eq), .Q(portio_1_p1), .clk(and_1_out));  // open: en, clr

  // Notes on the sheet:
  //   R0
  //   Renata Rodrigues Coelho - 22251140
  //   R1
  //   R2
  //   R3
endmodule

module enable (
  input  in_1,
  input  in_2,
  input  in_3,
  input  in_4,
  input  in_5,
  input  in_6,
  input  in_7,
  input  in_8,
  input  in_9,
  output out_10,
  output out_11,
  output out_12,
  output out_13,
  output out_14,
  output out_15,
  output out_16,
  output out_17
);

  and and_1 (out_10, in_1, in_9);
  and and_2 (out_11, in_2, in_9);
  and and_3 (out_12, in_3, in_9);
  and and_4 (out_13, in_4, in_9);
  and and_5 (out_14, in_5, in_9);
  and and_6 (out_15, in_6, in_9);
  and and_7 (out_16, in_7, in_9);
  and and_8 (out_17, in_8, in_9);
endmodule

module decoder2x4 (
  input  in_1,
  input  in_2,
  output out_3,
  output out_4,
  output out_5,
  output out_6
);

  wire not_1_out, not_2_out;

  not not_1 (not_1_out, in_1);
  not not_2 (not_2_out, in_2);
  and and_1 (out_3, not_1_out, not_2_out);
  and and_2 (out_4, in_1, not_2_out);
  and and_3 (out_5, not_1_out, in_2);
  and and_4 (out_6, in_1, in_2);
endmodule

module shift_R (
  input  in_1,
  input  [15:0] in_2,
  output [15:0] out_3,
  output out_4
);


  assign out_3 = {in_1, in_2[15:1]};
  assign out_4 = in_2[0];

  // Notes on the sheet:
  //   c_out
  //   c_in
endmodule

module shift_L (
  input  in_1,
  input  [15:0] in_2,
  output [15:0] out_3,
  output out_4
);


  assign out_3 = {in_2[14:0], in_1};
  assign out_4 = in_2[15];

  // Notes on the sheet:
  //   c_out
  //   c_in
endmodule

module ULA (
  input  [2:0] operacao,
  input  [15:0] A,
  input  [15:0] B,
  output c_out,
  output [15:0] resultado,
  output a_larger_than_b,
  output a_equal_b,
  output zero
);

  wire adder_1_cout, s_right_out_4, shift_l_1_out_4;
  wire [15:0] adder_1_out, and_1_out, not_1_out, or_1_out, s_right_out_3, shift_l_1_out_3, xor_1_out;

  shift_R s_right (.in_2(A), .in_1(1'b0), .out_4(s_right_out_4), .out_3(s_right_out_3));
  shift_L shift_l_1 (.in_2(A), .in_1(1'b0), .out_4(shift_l_1_out_4), .out_3(shift_l_1_out_3));
  assign not_1_out = ~A;  // NOT_Gate not_1, 16 bits wide
  assign and_1_out = A & B;  // AND_Gate and_1, 16 bits wide
  assign or_1_out = A | B;  // OR_Gate or_1, 16 bits wide
  Adder #(.width(16)) adder_1 (.a(A), .b(B), .out(adder_1_out), .cin(1'b0), .cout(adder_1_cout));
  assign xor_1_out = A ^ B;  // XOR_Gate xor_1, 16 bits wide
  Comparator #(.width(16)) comparator_1 (.a(A), .b(B), .gt(a_larger_than_b), .eq(a_equal_b));  // open: lt
  Multiplexer #(.select(3), .width(16)) multiplexer_1 (
    .in0(adder_1_out), .in1(s_right_out_3), .in2(shift_l_1_out_3), .in3(not_1_out), .in4(and_1_out),
    .in5(or_1_out), .in6(xor_1_out), .in7(A), .out(resultado), .sel(operacao));
  Multiplexer #(.select(3)) multiplexer_2 (
    .in0(adder_1_cout), .in1(s_right_out_4), .in2(shift_l_1_out_4), .in3(1'b0), .in4(1'b0), .in5(1'b0),
    .in6(1'b0), .in7(1'b0), .out(c_out), .sel(operacao));
  nor nor_1 (zero, resultado[0], resultado[1], resultado[2], resultado[3], resultado[4], resultado[5], resultado[6], resultado[7], resultado[8], resultado[9], resultado[10], resultado[11], resultado[12], resultado[13], resultado[14], resultado[15]);

  // Notes on the sheet:
  //   s_left
endmodule

module clk (
  output set,
  output enable
);

  wire clk_out, not_1_out, t_ff_1_q;

  Clock clk (.out(clk_out));
  not not_1 (not_1_out, clk_out);
  T_Flip_Flop t_ff_1 (.clk(clk_out), .T(1'b1), .Q(t_ff_1_q));  // open: Qn, preset, reset
  and and_1 (set, not_1_out, t_ff_1_q);
  or or_1 (enable, t_ff_1_q, clk_out);
endmodule

// s1
module stepper (
  output init,
  output s1,
  output s2,
  output s3,
  output s4,
  output s5,
  output s6
);

  wire clk_1_enable, decoder_1_out7;
  wire [2:0] counter_1_q;

  clk clk_1 (.enable(clk_1_enable));  // open: set
  Counter #(.max('h7), .width(3)) counter_1 (
    .D(3'b000), .Q(counter_1_q), .clk(clk_1_enable), .clr(decoder_1_out7));  // open: load, count, carry, up
  Decoder #(.enable("false"), .select(3)) decoder_1 (
    .out0(init), .out1(s1), .out2(s2), .out3(s3), .out4(s4), .out5(s5), .out6(s6), .out7(decoder_1_out7),
    .sel(counter_1_q));

  // Notes on the sheet:
  //   uma execução é realizada em 6 steps (ciclos)
endmodule

module bus_1 (
  input  [15:0] in_1,
  input  in_2,
  output [15:0] out_3
);

  Multiplexer #(.width(16)) multiplexer_1 (.in0(in_1), .in1(16'h1), .out(out_3), .sel(in_2));
endmodule

module UC (
  input  c_out,
  input  a_larger,
  input  equal,
  input  zero,
  input  [15:0] from_IR,
  output Bus1e,
  output TMPs,
  output R0s,
  output R0e,
  output R1s,
  output R1e,
  output R2s,
  output R2e,
  output R3s,
  output R3e,
  output MARs,
  output [2:0] to_ULA,
  output RAMs,
  output RAMe,
  output init,
  output flagss,
  output ACCs,
  output ACCe,
  output IARs,
  output IARe,
  output IRs,
  output Data_Address,
  output Ioe,
  output IOs,
  output Input_Output
);

  wire A_out, and_8_out, and_9_out, and_10_out, and_11_out, and_12_out, and_13_out, and_14_out, and_15_out,
       and_16_out, and_17_out, and_18_out, and_19_out, and_20_out, and_21_out, and_22_out, and_23_out,
       and_24_out, and_25_out, and_26_out, and_27_out, C_out_2, clk_1_enable, clk_1_set, d3x8_1_out_5,
       d3x8_1_out_6, d3x8_1_out_7, d3x8_1_out_8, d3x8_1_out_9, d3x8_1_out_10, d3x8_1_out_11, d3x8_1_out_12,
       d3x8_1_out_13, decoder2x4_1_out_3, decoder2x4_1_out_4, decoder2x4_1_out_5, decoder2x4_1_out_6, E_out,
       not_1_out, not_2_out, or_2_out, or_3_out, or_4_out, or_5_out, or_6_out, or_7_out, or_8_out, or_9_out,
       or_10_out, or_11_out, or_12_out, s1, s2, s3, s4, s5, s6, Z_out;

  clk clk_1 (.set(clk_1_set), .enable(clk_1_enable));
  and and_1 (IARe, clk_1_enable, or_2_out);
  and and_2 (RAMe, clk_1_enable, or_3_out);
  and and_3 (ACCe, clk_1_enable, or_4_out);
  and and_4 (Ioe, clk_1_enable, and_24_out);
  or or_1 (Bus1e, s1, and_16_out, and_15_out, and_12_out);
  or or_2 (or_2_out, s1, and_12_out, and_14_out, and_15_out);
  or or_3 (or_3_out, s2, and_27_out, and_22_out, and_21_out, and_19_out);
  or or_4 (or_4_out, s3, and_23_out, and_26_out, and_25_out);
  or or_5 (or_5_out, and_9_out, and_20_out, and_13_out, and_17_out);
  or or_6 (or_6_out, and_11_out, and_10_out, and_18_out);
  ra_rb_e ra_rb_e_1 (
    .out_8(R0e), .out_9(R1e), .out_10(R2e), .out_11(R3e), .a(clk_1_enable), .rb(or_5_out), .ra(or_6_out),
    .in_4(from_IR[0]), .in_5(from_IR[1]), .in_6(from_IR[2]), .in_7(from_IR[3]));
  and and_5 (to_ULA[0], s5, from_IR[15], from_IR[12]);
  and and_6 (to_ULA[1], s5, from_IR[15], from_IR[13]);
  and and_7 (to_ULA[2], s5, from_IR[15], from_IR[14]);
  d3X8 d3x8_1 (
    .out_5(d3x8_1_out_5), .in_1(from_IR[15]), .in_2(from_IR[14]), .in_3(from_IR[13]), .in_4(from_IR[12]),
    .out_6(d3x8_1_out_6), .out_7(d3x8_1_out_7), .out_8(d3x8_1_out_8), .out_9(d3x8_1_out_9),
    .out_10(d3x8_1_out_10), .out_11(d3x8_1_out_11), .out_12(d3x8_1_out_12), .out_13(d3x8_1_out_13));
  and C (C_out_2, from_IR[3], c_out);
  and A (A_out, from_IR[2], a_larger);
  and E (E_out, from_IR[1], equal);
  and Z (Z_out, from_IR[0], zero);
  and and_8 (and_8_out, from_IR[12], from_IR[13], from_IR[14]);
  not not_1 (not_1_out, and_8_out);
  stepper stepper_1 (.init(init), .s1(s1), .s2(s2), .s3(s3), .s4(s4), .s5(s5), .s6(s6));
  and and_9 (and_9_out, s4, d3x8_1_out_5);
  and and_10 (and_10_out, s4, d3x8_1_out_6);
  and and_11 (and_11_out, s4, d3x8_1_out_7);
  and and_12 (and_12_out, s4, d3x8_1_out_8);
  and and_13 (and_13_out, s4, d3x8_1_out_9);
  and and_14 (and_14_out, s4, d3x8_1_out_10);
  and and_15 (and_15_out, s4, d3x8_1_out_11);
  and and_16 (and_16_out, s4, d3x8_1_out_12);
  and and_17 (and_17_out, s4, d3x8_1_out_13, from_IR[3]);
  not not_2 (not_2_out, from_IR[3]);
  and and_18 (and_18_out, s5, d3x8_1_out_5);
  and and_19 (and_19_out, s5, d3x8_1_out_6);
  and and_20 (and_20_out, s5, d3x8_1_out_7);
  and and_21 (and_21_out, s5, d3x8_1_out_8);
  and and_22 (and_22_out, s5, d3x8_1_out_10);
  and and_23 (and_23_out, s5, d3x8_1_out_11);
  and and_24 (and_24_out, s5, d3x8_1_out_13, not_2_out);
  or or_7 (or_7_out, C_out_2, A_out, E_out, Z_out);
  and and_25 (and_25_out, s6, d3x8_1_out_5, not_1_out);
  and and_26 (and_26_out, s6, d3x8_1_out_8);
  and and_27 (and_27_out, s6, d3x8_1_out_11, or_7_out);
  decoder2x4 decoder2x4_1 (
    .in_1(from_IR[0]), .in_2(from_IR[1]), .out_3(decoder2x4_1_out_3), .out_4(decoder2x4_1_out_4),
    .out_5(decoder2x4_1_out_5), .out_6(decoder2x4_1_out_6));
  or or_8 (or_8_out, s1, and_12_out, and_15_out, and_10_out, and_11_out, and_14_out);
  or or_9 (or_9_out, s3, and_13_out, and_22_out, and_23_out, and_26_out, and_27_out);
  or or_10 (or_10_out, s1, and_12_out, and_15_out, and_18_out);
  or or_11 (or_11_out, and_16_out, and_18_out);
  or or_12 (or_12_out, and_19_out, and_25_out, and_21_out, and_24_out);
  and and_28 (IRs, clk_1_set, s2);
  and and_29 (MARs, clk_1_set, or_8_out);
  and and_30 (IARs, clk_1_set, or_9_out);
  and and_31 (ACCs, clk_1_set, or_10_out);
  and and_32 (RAMs, clk_1_set, and_20_out);
  and and_33 (TMPs, clk_1_set, and_9_out);
  and and_34 (flagss, clk_1_set, or_11_out);
  and and_35 (IOs, clk_1_set, and_17_out);
  and and_36 (R0s, clk_1_set, or_12_out, decoder2x4_1_out_3);
  and and_37 (R1s, clk_1_set, or_12_out, decoder2x4_1_out_4);
  and and_38 (R2s, clk_1_set, or_12_out, decoder2x4_1_out_5);
  and and_39 (R3s, clk_1_set, or_12_out, decoder2x4_1_out_6);

  assign Data_Address = from_IR[2];
  assign Input_Output = from_IR[3];
endmodule

module flags (
  input  c_out,
  input  larger,
  input  equal,
  input  set,
  input  zero,
  output out_6,
  output out_7,
  output out_8,
  output out_9
);

  Register #(.width(4)) register_1 (
    .D({zero, equal, larger, c_out}), .Q({out_9, out_8, out_7, out_6}), .clk(set));  // open: en, clr
endmodule

module ra_rb_e (
  input  a,
  input  rb,
  input  ra,
  input  in_4,
  input  in_5,
  input  in_6,
  input  in_7,
  output out_8,
  output out_9,
  output out_10,
  output out_11
);

  wire and_1_out, and_2_out, and_3_out, and_4_out, and_5_out, and_6_out, and_7_out, and_8_out,
       decoder_1_out0, decoder_1_out1, decoder_1_out2, decoder_1_out3, decoder_2_out0, decoder_2_out1,
       decoder_2_out2, decoder_2_out3;

  or or_1 (out_8, and_1_out, and_5_out);
  or or_2 (out_9, and_2_out, and_6_out);
  or or_3 (out_10, and_3_out, and_7_out);
  or or_4 (out_11, and_4_out, and_8_out);
  and and_1 (and_1_out, a, rb, decoder_1_out0);
  and and_2 (and_2_out, a, rb, decoder_1_out1);
  and and_3 (and_3_out, a, rb, decoder_1_out2);
  and and_4 (and_4_out, a, rb, decoder_1_out3);
  and and_5 (and_5_out, a, ra, decoder_2_out0);
  and and_6 (and_6_out, a, ra, decoder_2_out1);
  and and_7 (and_7_out, a, ra, decoder_2_out2);
  and and_8 (and_8_out, a, ra, decoder_2_out3);
  Decoder #(.enable("false"), .select(2)) decoder_1 (
    .out0(decoder_1_out0), .out1(decoder_1_out1), .out2(decoder_1_out2), .out3(decoder_1_out3),
    .sel({in_5, in_4}));
  Decoder #(.enable("false"), .select(2)) decoder_2 (
    .out0(decoder_2_out0), .out1(decoder_2_out1), .out2(decoder_2_out2), .out3(decoder_2_out3),
    .sel({in_7, in_6}));
endmodule

module d3X8 (
  input  in_1,
  input  in_2,
  input  in_3,
  input  in_4,
  output out_5,
  output out_6,
  output out_7,
  output out_8,
  output out_9,
  output out_10,
  output out_11,
  output out_12,
  output out_13
);

  wire decoder_1_out0, decoder_1_out1, decoder_1_out2, decoder_1_out3, decoder_1_out4, decoder_1_out5,
       decoder_1_out6, decoder_1_out7, not_1_out;

  not not_1 (not_1_out, in_1);
  Decoder #(.enable("false"), .select(3)) decoder_1 (
    .out0(decoder_1_out0), .out1(decoder_1_out1), .out2(decoder_1_out2), .out3(decoder_1_out3),
    .out4(decoder_1_out4), .out5(decoder_1_out5), .out6(decoder_1_out6), .out7(decoder_1_out7),
    .sel({in_2, in_3, in_4}));
  and and_1 (out_6, not_1_out, decoder_1_out0);
  and and_2 (out_7, not_1_out, decoder_1_out1);
  and and_3 (out_8, not_1_out, decoder_1_out2);
  and and_4 (out_9, not_1_out, decoder_1_out3);
  and and_5 (out_10, not_1_out, decoder_1_out4);
  and and_6 (out_11, not_1_out, decoder_1_out5);
  and and_7 (out_12, not_1_out, decoder_1_out6);
  and and_8 (out_13, not_1_out, decoder_1_out7);

  assign out_5 = in_1;
endmodule

module teclado (
  input  [15:0] in_1,
  input  in_2,
  input  [6:0] in_3,
  input  in_4,
  input  in_5,
  input  in_6,
  output [15:0] out_7,
  output out_8,
  output out_9
);

  wire and_1_out, comparator_1_eq;
  wire [15:0] bit_extender_1_out;

  Comparator #(.width(16)) comparator_1 (.a(in_1), .b({16{1'b0}}), .eq(comparator_1_eq));  // open: gt, lt
  T_Flip_Flop t_ff_1 (.clk(in_2), .T(1'b0), .Qn(out_8));  // open: Q, preset, reset
  Register #(.width(1)) register_1 (.D(comparator_1_eq), .Q(out_9), .clk(and_1_out));  // open: en, clr
  and and_1 (and_1_out, in_4, in_5, in_6);
  assign out_7 = in_2 ? bit_extender_1_out : 16'bz;  // Controlled_Buffer controlled_buffer_1
  assign bit_extender_1_out = {{9{1'b0}}, in_3};  // Bit_Extender bit_extender_1
endmodule

module monitor (
  input  [15:0] in_1,
  input  in_2,
  input  in_3,
  input  in_4,
  output [6:0] out_5,
  output out_6,
  output out_7
);

  wire and_1_out, comparator_1_eq;

  Bit_Extender #(.in_width(16), .out_width(7)) bit_extender_1 (.in(in_1), .out(out_5));
  Comparator #(.width(16)) comparator_1 (.a(in_1), .b(16'h1), .eq(comparator_1_eq));  // open: gt, lt
  Register #(.width(1)) register_1 (.D(comparator_1_eq), .Q(out_7), .clk(and_1_out));  // open: en, clr
  and and_1 (and_1_out, in_2, in_3, in_4);

  assign out_6 = in_2;
endmodule
